# Fritzing sketch Untitled Sketch 2 (saved by Fritzing 0.9.3b)
circuit board: 5.17201cm x 2.34978cm
breadboards: 1

parts:
  Feather_M0_Bluefruit_LE = Adafruit Feather M0 Express [part_number="Adafruit #3403"]
  RGB_LED = RGB LED (com. anode, rbg) [package="5 mm [THT]"]

nets:
  N1: Feather_M0_Bluefruit_LE.GND, RGB_LED.common_anode
  N2: Feather_M0_Bluefruit_LE.D9, RGB_LED.red_cathode
  N3: Feather_M0_Bluefruit_LE.D6, RGB_LED.blue_cathode
  N4: Feather_M0_Bluefruit_LE.D5, RGB_LED.green_cathode

custom parts:
  Adafruit Feather M0 Express: We love all our Feathers equally, but this Feather is very special. It's our first Feather that is specifically designed for use with CircuitPython! CircuitPython is our beginner-oriented flavor of MicroPython - and as the name hints at, its a small but full-featured version of the popular Python programming language specifically for use with circuitry and electronics. That doesn't mean you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
